// Logisim project ex5.circ as structural Verilog: 1 circuit, main circuit RotLeft
module RotLeft (
  input  [15:0] INPUT0,
  input  [3:0] AMOUNT,
  output [15:0] out_3
);

  wire multiplexer_1_out, multiplexer_2_out, multiplexer_3_out, multiplexer_4_out, multiplexer_5_out,
       multiplexer_6_out, multiplexer_7_out, multiplexer_8_out, multiplexer_9_out, multiplexer_10_out,
       multiplexer_11_out, multiplexer_12_out, multiplexer_13_out, multiplexer_14_out, multiplexer_15_out,
       multiplexer_16_out, multiplexer_17_out, multiplexer_18_out, multiplexer_19_out, multiplexer_20_out,
       multiplexer_21_out, multiplexer_22_out, multiplexer_23_out, multiplexer_24_out, multiplexer_25_out,
       multiplexer_26_out, multiplexer_27_out, multiplexer_28_out, multiplexer_29_out, multiplexer_30_out,
       multiplexer_31_out, multiplexer_32_out, multiplexer_33_out, multiplexer_34_out, multiplexer_35_out,
       multiplexer_36_out, multiplexer_37_out, multiplexer_38_out, multiplexer_39_out, multiplexer_40_out,
       multiplexer_41_out, multiplexer_42_out, multiplexer_43_out, multiplexer_44_out, multiplexer_45_out,
       multiplexer_46_out, multiplexer_47_out, multiplexer_48_out;

  Multiplexer #(.enable("false")) multiplexer_1 (
    .in0(INPUT0[0]), .in1(INPUT0[8]), .out(multiplexer_1_out), .sel(AMOUNT[3]));
  Multiplexer #(.enable("false")) multiplexer_2 (
    .in0(INPUT0[1]), .in1(INPUT0[9]), .out(multiplexer_2_out), .sel(AMOUNT[3]));
  Multiplexer #(.enable("false")) multiplexer_3 (
    .in0(INPUT0[2]), .in1(INPUT0[10]), .out(multiplexer_3_out), .sel(AMOUNT[3]));
  Multiplexer #(.enable("false")) multiplexer_4 (
    .in0(INPUT0[3]), .in1(INPUT0[11]), .out(multiplexer_4_out), .sel(AMOUNT[3]));
  Multiplexer #(.enable("false")) multiplexer_5 (
    .in0(INPUT0[4]), .in1(INPUT0[12]), .out(multiplexer_5_out), .sel(AMOUNT[3]));
  Multiplexer #(.enable("false")) multiplexer_6 (
    .in0(INPUT0[5]), .in1(INPUT0[13]), .out(multiplexer_6_out), .sel(AMOUNT[3]));
  Multiplexer #(.enable("false")) multiplexer_7 (
    .in0(INPUT0[6]), .in1(INPUT0[14]), .out(multiplexer_7_out), .sel(AMOUNT[3]));
  Multiplexer #(.enable("false")) multiplexer_8 (
    .in0(INPUT0[7]), .in1(INPUT0[15]), .out(multiplexer_8_out), .sel(AMOUNT[3]));
  Multiplexer #(.enable("false")) multiplexer_9 (
    .in0(INPUT0[8]), .in1(INPUT0[0]), .out(multiplexer_9_out), .sel(AMOUNT[3]));
  Multiplexer #(.enable("false")) multiplexer_10 (
    .in0(INPUT0[9]), .in1(INPUT0[1]), .out(multiplexer_10_out), .sel(AMOUNT[3]));
  Multiplexer #(.enable("false")) multiplexer_11 (
    .in0(INPUT0[10]), .in1(INPUT0[2]), .out(multiplexer_11_out), .sel(AMOUNT[3]));
  Multiplexer #(.enable("false")) multiplexer_12 (
    .in0(INPUT0[11]), .in1(INPUT0[3]), .out(multiplexer_12_out), .sel(AMOUNT[3]));
  Multiplexer #(.enable("false")) multiplexer_13 (
    .in0(INPUT0[12]), .in1(INPUT0[4]), .out(multiplexer_13_out), .sel(AMOUNT[3]));
  Multiplexer #(.enable("false")) multiplexer_14 (
    .in0(INPUT0[13]), .in1(INPUT0[5]), .out(multiplexer_14_out), .sel(AMOUNT[3]));
  Multiplexer #(.enable("false")) multiplexer_15 (
    .in0(INPUT0[14]), .in1(INPUT0[6]), .out(multiplexer_15_out), .sel(AMOUNT[3]));
  Multiplexer #(.enable("false")) multiplexer_16 (
    .in0(INPUT0[15]), .in1(INPUT0[7]), .out(multiplexer_16_out), .sel(AMOUNT[3]));
  Multiplexer #(.enable("false")) multiplexer_17 (
    .in0(multiplexer_1_out), .in1(multiplexer_13_out), .out(multiplexer_17_out), .sel(AMOUNT[2]));
  Multiplexer #(.enable("false")) multiplexer_18 (
    .in0(multiplexer_2_out), .in1(multiplexer_14_out), .out(multiplexer_18_out), .sel(AMOUNT[2]));
  Multiplexer #(.enable("false")) multiplexer_19 (
    .in0(multiplexer_3_out), .in1(multiplexer_15_out), .out(multiplexer_19_out), .sel(AMOUNT[2]));
  Multiplexer #(.enable("false")) multiplexer_20 (
    .in0(multiplexer_4_out), .in1(multiplexer_16_out), .out(multiplexer_20_out), .sel(AMOUNT[2]));
  Multiplexer #(.enable("false")) multiplexer_21 (
    .in0(multiplexer_5_out), .in1(multiplexer_1_out), .out(multiplexer_21_out), .sel(AMOUNT[2]));
  Multiplexer #(.enable("false")) multiplexer_22 (
    .in0(multiplexer_6_out), .in1(multiplexer_2_out), .out(multiplexer_22_out), .sel(AMOUNT[2]));
  Multiplexer #(.enable("false")) multiplexer_23 (
    .in0(multiplexer_7_out), .in1(multiplexer_3_out), .out(multiplexer_23_out), .sel(AMOUNT[2]));
  Multiplexer #(.enable("false")) multiplexer_24 (
    .in0(multiplexer_8_out), .in1(multiplexer_4_out), .out(multiplexer_24_out), .sel(AMOUNT[2]));
  Multiplexer #(.enable("false")) multiplexer_25 (
    .in0(multiplexer_9_out), .in1(multiplexer_5_out), .out(multiplexer_25_out), .sel(AMOUNT[2]));
  Multiplexer #(.enable("false")) multiplexer_26 (
    .in0(multiplexer_10_out), .in1(multiplexer_6_out), .out(multiplexer_26_out), .sel(AMOUNT[2]));
  Multiplexer #(.enable("false")) multiplexer_27 (
    .in0(multiplexer_11_out), .in1(multiplexer_7_out), .out(multiplexer_27_out), .sel(AMOUNT[2]));
  Multiplexer #(.enable("false")) multiplexer_28 (
    .in0(multiplexer_12_out), .in1(multiplexer_8_out), .out(multiplexer_28_out), .sel(AMOUNT[2]));
  Multiplexer #(.enable("false")) multiplexer_29 (
    .in0(multiplexer_13_out), .in1(multiplexer_9_out), .out(multiplexer_29_out), .sel(AMOUNT[2]));
  Multiplexer #(.enable("false")) multiplexer_30 (
    .in0(multiplexer_14_out), .in1(multiplexer_10_out), .out(multiplexer_30_out), .sel(AMOUNT[2]));
  Multiplexer #(.enable("false")) multiplexer_31 (
    .in0(multiplexer_15_out), .in1(multiplexer_11_out), .out(multiplexer_31_out), .sel(AMOUNT[2]));
  Multiplexer #(.enable("false")) multiplexer_32 (
    .in0(multiplexer_16_out), .in1(multiplexer_12_out), .out(multiplexer_32_out), .sel(AMOUNT[2]));
  Multiplexer #(.enable("false")) multiplexer_33 (
    .in0(multiplexer_17_out), .in1(multiplexer_31_out), .out(multiplexer_33_out), .sel(AMOUNT[1]));
  Multiplexer #(.enable("false")) multiplexer_34 (
    .in0(multiplexer_18_out), .in1(multiplexer_32_out), .out(multiplexer_34_out), .sel(AMOUNT[1]));
  Multiplexer #(.enable("false")) multiplexer_35 (
    .in0(multiplexer_19_out), .in1(multiplexer_17_out), .out(multiplexer_35_out), .sel(AMOUNT[1]));
  Multiplexer #(.enable("false")) multiplexer_36 (
    .in0(multiplexer_20_out), .in1(multiplexer_18_out), .out(multiplexer_36_out), .sel(AMOUNT[1]));
  Multiplexer #(.enable("false")) multiplexer_37 (
    .in0(multiplexer_21_out), .in1(multiplexer_19_out), .out(multiplexer_37_out), .sel(AMOUNT[1]));
  Multiplexer #(.enable("false")) multiplexer_38 (
    .in0(multiplexer_22_out), .in1(multiplexer_20_out), .out(multiplexer_38_out), .sel(AMOUNT[1]));
  Multiplexer #(.enable("false")) multiplexer_39 (
    .in0(multiplexer_23_out), .in1(multiplexer_21_out), .out(multiplexer_39_out), .sel(AMOUNT[1]));
  Multiplexer #(.enable("false")) multiplexer_40 (
    .in0(multiplexer_24_out), .in1(multiplexer_22_out), .out(multiplexer_40_out), .sel(AMOUNT[1]));
  Multiplexer #(.enable("false")) multiplexer_41 (
    .in0(multiplexer_25_out), .in1(multiplexer_23_out), .out(multiplexer_41_out), .sel(AMOUNT[1]));
  Multiplexer #(.enable("false")) multiplexer_42 (
    .in0(multiplexer_26_out), .in1(multiplexer_24_out), .out(multiplexer_42_out), .sel(AMOUNT[1]));
  Multiplexer #(.enable("false")) multiplexer_43 (
    .in0(multiplexer_27_out), .in1(multiplexer_25_out), .out(multiplexer_43_out), .sel(AMOUNT[1]));
  Multiplexer #(.enable("false")) multiplexer_44 (
    .in0(multiplexer_28_out), .in1(multiplexer_26_out), .out(multiplexer_44_out), .sel(AMOUNT[1]));
  Multiplexer #(.enable("false")) multiplexer_45 (
    .in0(multiplexer_29_out), .in1(multiplexer_27_out), .out(multiplexer_45_out), .sel(AMOUNT[1]));
  Multiplexer #(.enable("false")) multiplexer_46 (
    .in0(multiplexer_30_out), .in1(multiplexer_28_out), .out(multiplexer_46_out), .sel(AMOUNT[1]));
  Multiplexer #(.enable("false")) multiplexer_47 (
    .in0(multiplexer_31_out), .in1(multiplexer_29_out), .out(multiplexer_47_out), .sel(AMOUNT[1]));
  Multiplexer #(.enable("false")) multiplexer_48 (
    .in0(multiplexer_32_out), .in1(multiplexer_30_out), .out(multiplexer_48_out), .sel(AMOUNT[1]));
  Multiplexer #(.enable("false")) multiplexer_49 (
    .in0(multiplexer_33_out), .in1(multiplexer_48_out), .out(out_3[0]), .sel(AMOUNT[0]));
  Multiplexer #(.enable("false")) multiplexer_50 (
    .in0(multiplexer_34_out), .in1(multiplexer_33_out), .out(out_3[1]), .sel(AMOUNT[0]));
  Multiplexer #(.enable("false")) multiplexer_51 (
    .in0(multiplexer_35_out), .in1(multiplexer_34_out), .out(out_3[2]), .sel(AMOUNT[0]));
  Multiplexer #(.enable("false")) multiplexer_52 (
    .in0(multiplexer_36_out), .in1(multiplexer_35_out), .out(out_3[3]), .sel(AMOUNT[0]));
  Multiplexer #(.enable("false")) multiplexer_53 (
    .in0(multiplexer_37_out), .in1(multiplexer_36_out), .out(out_3[4]), .sel(AMOUNT[0]));
  Multiplexer #(.enable("false")) multiplexer_54 (
    .in0(multiplexer_38_out), .in1(multiplexer_37_out), .out(out_3[5]), .sel(AMOUNT[0]));
  Multiplexer #(.enable("false")) multiplexer_55 (
    .in0(multiplexer_39_out), .in1(multiplexer_38_out), .out(out_3[6]), .sel(AMOUNT[0]));
  Multiplexer #(.enable("false")) multiplexer_56 (
    .in0(multiplexer_40_out), .in1(multiplexer_39_out), .out(out_3[7]), .sel(AMOUNT[0]));
  Multiplexer #(.enable("false")) multiplexer_57 (
    .in0(multiplexer_41_out), .in1(multiplexer_40_out), .out(out_3[8]), .sel(AMOUNT[0]));
  Multiplexer #(.enable("false")) multiplexer_58 (
    .in0(multiplexer_42_out), .in1(multiplexer_41_out), .out(out_3[9]), .sel(AMOUNT[0]));
  Multiplexer #(.enable("false")) multiplexer_59 (
    .in0(multiplexer_43_out), .in1(multiplexer_42_out), .out(out_3[10]), .sel(AMOUNT[0]));
  Multiplexer #(.enable("false")) multiplexer_60 (
    .in0(multiplexer_44_out), .in1(multiplexer_43_out), .out(out_3[11]), .sel(AMOUNT[0]));
  Multiplexer #(.enable("false")) multiplexer_61 (
    .in0(multiplexer_45_out), .in1(multiplexer_44_out), .out(out_3[12]), .sel(AMOUNT[0]));
  Multiplexer #(.enable("false")) multiplexer_62 (
    .in0(multiplexer_46_out), .in1(multiplexer_45_out), .out(out_3[13]), .sel(AMOUNT[0]));
  Multiplexer #(.enable("false")) multiplexer_63 (
    .in0(multiplexer_47_out), .in1(multiplexer_46_out), .out(out_3[14]), .sel(AMOUNT[0]));
  Multiplexer #(.enable("false")) multiplexer_64 (
    .in0(multiplexer_48_out), .in1(multiplexer_47_out), .out(out_3[15]), .sel(AMOUNT[0]));
endmodule
