// Logisim project Scheme1.circ as structural Verilog: 1 circuit, main circuit main
module main (
  input  L,
  input  R,
  input  CLK,
  input  Reset,
  output out_5,
  output out_6,
  output out_7,
  output out_8,
  output out_9,
  output out_10
);

  wire and_1_out, and_2_out, and_3_out, and_4_out, and_5_out, and_6_out, and_7_out, and_8_out, and_9_out,
       and_10_out, and_11_out, and_12_out, and_13_out, and_14_out, and_15_out, and_16_out, and_17_out,
       and_18_out;
  wire [3:0] Q0N_out, register_1_q;

  and and_1 (and_1_out, ~register_1_q[0], register_1_q[1], ~register_1_q[3]);  // AND_Gate
  and and_2 (and_2_out, ~register_1_q[0], register_1_q[2], ~register_1_q[3]);  // AND_Gate
  and and_3 (and_3_out, ~register_1_q[0], ~register_1_q[1], ~register_1_q[2], register_1_q[3]);  // AND_Gate
  and and_4 (and_4_out, L, ~R, ~register_1_q[0], ~register_1_q[3]);  // AND_Gate
  and and_5 (and_5_out, register_1_q[0], ~register_1_q[1], ~register_1_q[2]);  // AND_Gate
  and and_6 (and_6_out, ~register_1_q[0], register_1_q[1], ~register_1_q[3]);  // AND_Gate
  and and_7 (and_7_out, ~L, R, ~register_1_q[0], ~register_1_q[2], ~register_1_q[3]);  // AND_Gate
  and and_8 (and_8_out, ~register_1_q[0], register_1_q[2], ~register_1_q[3]);  // AND_Gate
  and and_9 (and_9_out, register_1_q[0], register_1_q[1], ~register_1_q[2], ~register_1_q[3]);  // AND_Gate
  and and_10 (and_10_out, ~L, R, ~register_1_q[0], ~register_1_q[1], ~register_1_q[3]);  // AND_Gate
  and and_11 (and_11_out, ~register_1_q[1], ~register_1_q[2], register_1_q[3]);  // AND_Gate
  and and_12 (and_12_out, register_1_q[0], register_1_q[1], register_1_q[2], ~register_1_q[3]);  // AND_Gate
  or Q0N (Q0N_out[0], and_1_out, and_2_out, and_3_out, and_4_out);
  or Q1N (Q0N_out[1], and_5_out, and_6_out, and_7_out);
  or Q2N (Q0N_out[2], and_8_out, and_9_out, and_10_out);
  or Q3N (Q0N_out[3], and_11_out, and_12_out);
  Register #(.width(4)) register_1 (.D(Q0N_out), .clk(CLK), .Q(register_1_q), .clr(Reset));  // open: en
  and LC (out_5, ~register_1_q[1], register_1_q[2], ~register_1_q[3]);  // AND_Gate
  and and_13 (and_13_out, register_1_q[0], register_1_q[1], ~register_1_q[2], ~register_1_q[3]);  // AND_Gate
  and and_14 (and_14_out, ~register_1_q[0], ~register_1_q[1], register_1_q[2], ~register_1_q[3]);  // AND_Gate
  and LA (out_7, register_1_q[1], ~register_1_q[2], ~register_1_q[3]);  // AND_Gate
  and and_15 (and_15_out, register_1_q[0], register_1_q[1], register_1_q[2], ~register_1_q[3]);  // AND_Gate
  and and_16 (and_16_out, ~register_1_q[0], ~register_1_q[1], ~register_1_q[2], register_1_q[3]);  // AND_Gate
  and RB (out_9, ~register_1_q[1], ~register_1_q[2], register_1_q[3]);  // AND_Gate
  and and_17 (and_17_out, register_1_q[0], ~register_1_q[1], ~register_1_q[2], register_1_q[3]);  // AND_Gate
  and and_18 (and_18_out, ~register_1_q[0], register_1_q[1], ~register_1_q[2], register_1_q[3]);  // AND_Gate
  or LB (out_6, and_13_out, and_14_out);
  or RA (out_8, and_15_out, and_16_out);
  or RC (out_10, and_17_out, and_18_out);
endmodule
